// Logisim project M.R.circ as structural Verilog: 1 circuit, main circuit main
module main (
  input  in_1,
  input  in_2,
  input  in_3,
  input  in_4,
  input  in_5,
  input  in_6,
  input  in_7,
  input  in_8,
  input  in_9,
  output out_10,
  output out_11,
  output out_12,
  output out_13
);

  wire nor_1_out;

  and and_1 (out_10, in_1, in_2);
  or or_1 (out_11, in_3, in_4);
  not not_1 (out_12, in_5);
  xor xor_1 (out_13, in_6, in_7);
  not nor_1 (nor_1_out, in_8);  // NOR_Gate
endmodule
